// Logisim project realALU.circ as structural Verilog: 10 circuits, main circuit main
module main (
  input  [3:0] aluOp,
  input  [7:0] inA,
  input  [7:0] inB,
  output [7:0] aluOut,
  output Z,
  output C,
  output N
);

  wire and_1_z__1_if_out____0x00, logicalshiftleft_1_c__1_if_out_8_____1,
       logicalshiftleft_1_n__1_if_out_7_____1, logicalshiftleft_1_z__1_if_out____0x00,
       logicalshiftright_1_c__1_if_out__1_____1, logicalshiftright_1_n__1_if_out_7_____1,
       logicalshiftright_1_z__1_if_out____0x00, not_1_out, not_2_z__1_if_out____0x00,
       or_1_z__1_if_out____0x00;
  wire [7:0] and_1_out, decoder8_1_output, decoder8_2_output, logicalshiftleft_1_out,
       logicalshiftright_1_out, not_2_out, or_1_out;

  decoder8 decoder8_1 (.Enable(not_1_out), .Select(aluOp[3:1]), .Output(decoder8_1_output));
  not not_1 (not_1_out, aluOp[0]);
  decoder8 decoder8_2 (.Enable(aluOp[0]), .Select(aluOp[3:1]), .Output(decoder8_2_output));
  AND and_1 (
    .inA(inA), .inB(inB), .out(and_1_out), .Enable(decoder8_1_output[0]),
    .Z__1_if_out____0x00(and_1_z__1_if_out____0x00));
  OR or_1 (
    .inA(inA), .inB(inB), .out(or_1_out), .Enable(decoder8_1_output[1]),
    .Z__1_if_out____0x00(or_1_z__1_if_out____0x00));
  NOT not_2 (.in(inB), .out(not_2_out), .Enable(decoder8_1_output[2]), .Z__1_if_out____0x00(not_2_z__1_if_out____0x00));
  logicalShiftRight logicalshiftright_1 (
    .in(inB), .out(logicalshiftright_1_out), .Enable(decoder8_1_output[3]),
    .Z__1_if_out____0x00(logicalshiftright_1_z__1_if_out____0x00),
    .C__1_if_out__1_____1(logicalshiftright_1_c__1_if_out__1_____1),
    .N__1_if_out_7_____1(logicalshiftright_1_n__1_if_out_7_____1));
  logicalShiftLeft logicalshiftleft_1 (
    .in(inB), .out(logicalshiftleft_1_out), .Enable(decoder8_1_output[4]),
    .C__1_if_out_8_____1(logicalshiftleft_1_c__1_if_out_8_____1),
    .N__1_if_out_7_____1(logicalshiftleft_1_n__1_if_out_7_____1),
    .Z__1_if_out____0x00(logicalshiftleft_1_z__1_if_out____0x00));
  or or_2 (C, logicalshiftright_1_c__1_if_out__1_____1, logicalshiftleft_1_c__1_if_out_8_____1);
  or or_3 (N, logicalshiftright_1_n__1_if_out_7_____1, logicalshiftleft_1_n__1_if_out_7_____1);
  assign aluOut = and_1_out | or_1_out | not_2_out | logicalshiftright_1_out | logicalshiftleft_1_out;  // OR_Gate or_4, 8 bits wide
  or or_5 (Z, and_1_z__1_if_out____0x00, or_1_z__1_if_out____0x00, not_2_z__1_if_out____0x00, logicalshiftright_1_z__1_if_out____0x00, logicalshiftleft_1_z__1_if_out____0x00);
endmodule

module AND (
  input  Enable,
  input  [7:0] inA,
  input  [7:0] inB,
  output [7:0] out,
  output Z__1_if_out____0x00
);

  wire nor_1_out;
  wire [7:0] and_1_out;

  assign and_1_out = inA & inB;  // AND_Gate and_1, 8 bits wide
  Transistor #(.\type ("n"), .width(8)) transistor_1 (.in(and_1_out), .out(out), .gate(Enable));
  Pull_Resistor pull_resistor_1 (.node(out));
  nor nor_1 (nor_1_out, and_1_out[0], and_1_out[1], and_1_out[2], and_1_out[3], and_1_out[4], and_1_out[5], and_1_out[6], and_1_out[7]);
  Pull_Resistor pull_resistor_2 (.node(Z__1_if_out____0x00));
  Transistor #(.\type ("n")) transistor_2 (.in(nor_1_out), .out(Z__1_if_out____0x00), .gate(Enable));
endmodule

module OR (
  input  Enable,
  input  [7:0] inA,
  input  [7:0] inB,
  output [7:0] out,
  output Z__1_if_out____0x00
);

  wire nor_1_out;
  wire [7:0] or_1_out;

  assign or_1_out = inA | inB;  // OR_Gate or_1, 8 bits wide
  Transistor #(.\type ("n"), .width(8)) transistor_1 (.in(or_1_out), .out(out), .gate(Enable));
  Pull_Resistor pull_resistor_1 (.node(out));
  nor nor_1 (nor_1_out, or_1_out[0], or_1_out[1], or_1_out[2], or_1_out[3], or_1_out[4], or_1_out[5], or_1_out[6], or_1_out[7]);
  Pull_Resistor pull_resistor_2 (.node(Z__1_if_out____0x00));
  Transistor #(.\type ("n")) transistor_2 (.in(nor_1_out), .out(Z__1_if_out____0x00), .gate(Enable));
endmodule

module NOT (
  input  Enable,
  input  [7:0] in,
  output [7:0] out,
  output Z__1_if_out____0x00
);

  wire nor_1_out;
  wire [7:0] not_1_out;

  assign not_1_out = ~in;  // NOT_Gate not_1, 8 bits wide
  Pull_Resistor pull_resistor_1 (.node(out));
  Transistor #(.\type ("n"), .width(8)) transistor_1 (.in(not_1_out), .out(out), .gate(Enable));
  nor nor_1 (nor_1_out, not_1_out[0], not_1_out[1], not_1_out[2], not_1_out[3], not_1_out[4], not_1_out[5], not_1_out[6], not_1_out[7]);
  Pull_Resistor pull_resistor_2 (.node(Z__1_if_out____0x00));
  Transistor #(.\type ("n")) transistor_2 (.in(nor_1_out), .out(Z__1_if_out____0x00), .gate(Enable));
endmodule

module logicalShiftRight (
  input  Enable,
  input  [7:0] in,
  output [7:0] out,
  output Z__1_if_out____0x00,
  output C__1_if_out__1_____1,
  output N__1_if_out_7_____1
);

  wire nor_1_out;

  Pull_Resistor pull_resistor_1 (.node(out));
  Transistor #(.\type ("n"), .width(8)) transistor_1 (.in({1'b0, in[7:1]}), .out(out), .gate(Enable));
  nor nor_1 (nor_1_out, in[1], in[2], in[3], in[4], in[5], in[6], in[7], 1'b0);
  Pull_Resistor pull_resistor_2 (.node(Z__1_if_out____0x00));
  Transistor #(.\type ("n")) transistor_2 (.in(nor_1_out), .out(Z__1_if_out____0x00), .gate(Enable));
  Pull_Resistor pull_resistor_3 (.node(C__1_if_out__1_____1));
  Transistor #(.\type ("n")) transistor_3 (.in(in[0]), .out(C__1_if_out__1_____1), .gate(Enable));
  Transistor #(.\type ("n")) transistor_4 (.in(1'b0), .out(N__1_if_out_7_____1), .gate(Enable));
  Pull_Resistor pull_resistor_4 (.node(N__1_if_out_7_____1));

  // Other names for the same wires on the sheet: C = in[0]
endmodule

module logicalShiftLeft (
  input  Enable,
  input  [7:0] in,
  output [7:0] out,
  output Z__1_if_out____0x00,
  output C__1_if_out_8_____1,
  output N__1_if_out_7_____1
);

  wire nor_1_out;

  Pull_Resistor pull_resistor_1 (.node(out));
  Transistor #(.\type ("n"), .width(8)) transistor_1 (.in({in[6:0], 1'b0}), .out(out), .gate(Enable));
  nor nor_1 (nor_1_out, 1'b0, in[0], in[1], in[2], in[3], in[4], in[5], in[6]);
  Pull_Resistor pull_resistor_2 (.node(Z__1_if_out____0x00));
  Transistor #(.\type ("n")) transistor_2 (.in(nor_1_out), .out(Z__1_if_out____0x00), .gate(Enable));
  Pull_Resistor pull_resistor_3 (.node(C__1_if_out_8_____1));
  Transistor #(.\type ("n")) transistor_3 (.in(in[7]), .out(C__1_if_out_8_____1), .gate(Enable));
  Transistor #(.\type ("n")) transistor_4 (.in(in[6]), .out(N__1_if_out_7_____1), .gate(Enable));
  Pull_Resistor pull_resistor_4 (.node(N__1_if_out_7_____1));

  // Other names for the same wires on the sheet: C = in[7]
endmodule

module decoder8 (
  input  Enable,
  input  [2:0] Select,
  output [7:0] Output
);

  wire [7:0] and_1_out;

  and and_1 (and_1_out[0], ~Select[0], ~Select[1], ~Select[2]);  // AND_Gate
  and and_2 (and_1_out[1], Select[0], ~Select[1], ~Select[2]);  // AND_Gate
  and and_3 (and_1_out[2], ~Select[0], Select[1], ~Select[2]);  // AND_Gate
  and and_4 (and_1_out[3], Select[0], Select[1], ~Select[2]);  // AND_Gate
  and and_5 (and_1_out[4], ~Select[0], ~Select[1], Select[2]);  // AND_Gate
  and and_6 (and_1_out[5], Select[0], ~Select[1], Select[2]);  // AND_Gate
  and and_7 (and_1_out[6], ~Select[0], Select[1], Select[2]);  // AND_Gate
  and and_8 (and_1_out[7], Select[0], Select[1], Select[2]);
  Pull_Resistor pull_resistor_1 (.node(Output));
  Transistor #(.\type ("n"), .width(8)) transistor_1 (.in(and_1_out), .out(Output), .gate(Enable));
endmodule

module Full_Adder (
  input  inA,
  input  inB,
  input  CarryIn,
  output Output,
  output CarryOut
);

  wire and_1_out, and_2_out, and_3_out, xor_1_out;

  xor xor_1 (xor_1_out, inA, inB);
  and and_1 (and_1_out, inA, inB);
  and and_2 (and_2_out, inB, CarryIn);
  and and_3 (and_3_out, inA, CarryIn);
  xor xor_2 (Output, xor_1_out, CarryIn);
  or or_1 (CarryOut, and_1_out, and_2_out, and_3_out);
endmodule

module Alsum (
  input  [7:0] inA,
  input  [7:0] inB,
  input  Enable,
  output [7:0] Output,
  output Z,
  output V,
  output S,
  output C
);

  wire full_adder_1_carryout, full_adder_2_carryout, full_adder_3_carryout, full_adder_4_carryout,
       full_adder_5_carryout, full_adder_6_carryout, full_adder_7_carryout, nor_1_out;

  Full_Adder full_adder_1 (
    .inA(inA[0]), .inB(inB[0]), .CarryIn(inB[0]), .Output(Output[0]), .CarryOut(full_adder_1_carryout));
  Full_Adder full_adder_2 (
    .inA(inA[1]), .inB(inB[1]), .CarryIn(full_adder_1_carryout), .Output(Output[1]),
    .CarryOut(full_adder_2_carryout));
  Full_Adder full_adder_3 (
    .inA(inA[2]), .inB(inB[2]), .CarryIn(full_adder_2_carryout), .Output(Output[2]),
    .CarryOut(full_adder_3_carryout));
  Full_Adder full_adder_4 (
    .inA(inA[3]), .inB(inB[3]), .CarryIn(full_adder_3_carryout), .Output(Output[3]),
    .CarryOut(full_adder_4_carryout));
  Full_Adder full_adder_5 (
    .inA(inA[4]), .inB(inB[4]), .CarryIn(full_adder_4_carryout), .Output(Output[4]),
    .CarryOut(full_adder_5_carryout));
  Full_Adder full_adder_6 (
    .inA(inA[5]), .inB(inB[5]), .CarryIn(full_adder_5_carryout), .Output(Output[5]),
    .CarryOut(full_adder_6_carryout));
  Full_Adder full_adder_7 (
    .inA(inA[6]), .inB(inB[6]), .CarryIn(full_adder_6_carryout), .Output(Output[6]),
    .CarryOut(full_adder_7_carryout));
  Full_Adder full_adder_8 (
    .inA(inA[7]), .inB(inB[7]), .CarryIn(full_adder_7_carryout), .Output(Output[7]), .CarryOut(C));
  nor nor_1 (nor_1_out, Output[0], Output[1], Output[2], Output[3], Output[4], Output[5], Output[6], Output[7]);
  Transistor #(.\type ("n")) transistor_1 (.in(nor_1_out), .out(Z), .gate(Enable));
  nor nor_2 (V, Output[7], C);
  Pull_Resistor pull_resistor_1 (.node(Z));

  assign S = Output[7];
endmodule

module _2Components (
  input  [7:0] in,
  output [7:0] out
);

  wire [7:0] not_8_out;

  not not_1 (not_8_out[6], in[6]);
  not not_2 (not_8_out[4], in[4]);
  not not_3 (not_8_out[5], in[5]);
  not not_4 (not_8_out[7], in[7]);
  not not_5 (not_8_out[1], in[1]);
  not not_6 (not_8_out[2], in[2]);
  not not_7 (not_8_out[3], in[3]);
  not not_8 (not_8_out[0], in[0]);
  Alsum alsum_1 (.inA(not_8_out), .inB(8'h1), .Enable(1'b0), .Output(out));  // open: Z, V, S, C
endmodule
